// Logisim project Piloufas.circ as structural Verilog: 4 circuits, main circuit main
module main (
);

  wire button_1_out, button_2_out, button_3_out, button_4_out;

  Button button_1 (.out(button_1_out));
  Button button_2 (.out(button_2_out));
  Button button_3 (.out(button_3_out));
  Button button_4 (.out(button_4_out));
  button_input button_input_1 (
    .A(button_1_out), .B(button_2_out), .C(button_3_out), .R(button_4_out));  // open: A_st, A_lg, B_st, B_lg, C_st, C_lg
  output_display output_display_1 ();  // open: i_1, i_2, i_3, i_4, nxt, R, o
endmodule

module press (
  input  b_in,
  input  R,
  output st,
  output lg
);

  wire clock_1_out, counter_1_carry, counter_2_carry, d_ff_1_q, d_ff_2_q, not_1_out, not_2_out, not_3_out,
       or_1_out, or_2_out, or_3_out, or_4_out;

  Clock clock_1 (.out(clock_1_out));
  D_Flip_Flop #(.trigger("falling")) d_ff_1 (
    .D(not_1_out), .clk(b_in), .Q(d_ff_1_q), .reset(or_3_out));  // open: Qn, preset
  not not_1 (not_1_out, counter_1_carry);
  D_Flip_Flop #(.trigger("falling")) d_ff_2 (
    .D(counter_1_carry), .clk(b_in), .Q(d_ff_2_q), .reset(or_3_out));  // open: Qn, preset
  or or_1 (or_1_out, counter_2_carry, R);
  or or_2 (or_2_out, b_in, R);
  or or_3 (or_3_out, R, counter_2_carry);
  Counter #(.width(2), .max('h3), .ongoal("stay")) counter_1 (
    .clr(or_1_out), .count(b_in), .clk(clock_1_out), .carry(counter_1_carry));  // open: load, up, D, Q
  Counter #(.width(2), .max('h3), .ongoal("stay")) counter_2 (
    .clr(or_2_out), .count(or_4_out), .clk(clock_1_out), .carry(counter_2_carry));  // open: load, up, D, Q
  or or_4 (or_4_out, d_ff_1_q, d_ff_2_q);
  not not_2 (not_2_out, counter_1_carry);
  not not_3 (not_3_out, d_ff_1_q);
  and and_1 (st, d_ff_1_q, not_2_out);
  and and_2 (lg, counter_1_carry, not_3_out);
endmodule

module button_input (
  input  A,
  input  B,
  input  C,
  input  R,
  output A_st,
  output A_lg,
  output B_st,
  output B_lg,
  output C_st,
  output C_lg
);

  press press_1 (.b_in(A), .R(R), .st(A_st), .lg(A_lg));
  press press_2 (.b_in(B), .R(R), .st(B_st), .lg(B_lg));
  press press_3 (.b_in(C), .R(R), .st(C_st), .lg(C_lg));
endmodule

module output_display (
  input  i_1,
  input  i_2,
  input  i_3,
  input  i_4,
  input  nxt,
  input  R,
  output o
);

  wire d_ff_1_qn, d_ff_2_qn;
  wire [1:0] d_ff_1_q;

  D_Flip_Flop #(.trigger("falling")) d_ff_1 (
    .D(d_ff_1_qn), .clk(nxt), .Q(d_ff_1_q[0]), .Qn(d_ff_1_qn), .reset(R));  // open: preset
  Multiplexer #(.select(2), .enable("false")) multiplexer_1 (
    .in0(i_1), .in1(i_2), .in2(i_3), .in3(i_4), .out(o), .sel(d_ff_1_q));
  D_Flip_Flop #(.trigger("falling")) d_ff_2 (
    .D(d_ff_2_qn), .clk(d_ff_1_q[0]), .Q(d_ff_1_q[1]), .Qn(d_ff_2_qn), .reset(R));  // open: preset
endmodule
